# Fritzing sketch plotter_motors (saved by Fritzing 0.9.0b)
circuit board: 6.99757cm x 5.46765cm

parts:
  DC24V = Power Jack [package=power_jack_pth]
  5Vto3V = Logic Level Converter
  S2 = SWITCH-MOMENTARY-2 [package=tactile-pth]
  S3 = SWITCH-MOMENTARY-2 [package=tactile-pth]
  S4 = SWITCH-MOMENTARY-2 [package=tactile-pth]
  U1 = RJ45 Jack [package=rj45-8]
  S1 = SWITCH-MOMENTARY-2 [package=tactile-pth]
  R1 = Resistor [tolerance=±5% resistance=1k package=THT]
  R2 = Resistor [tolerance=±5% resistance=1k package=THT]
  R3 = Resistor [tolerance=±5% resistance=1k package=THT]
  R4 = Resistor [tolerance=±5% resistance=1k package=THT]
  Part1 = Arduino Uno (Rev3)
  BTM-112 = BTM-112
  J1 = male pin header, 3 pins [form="♂ (male)"]
  U2 = RJ45 Jack [package=rj45-8]
  LED1 = LED - 3mm [color="Red (633nm)" package="3 mm [THT]"]
  LED2 = LED - 3mm [color="Green (565nm)" package="3 mm [THT]"]
  R5 = Resistor [tolerance=±5% resistance=220 package=THT]
  R6 = Resistor [tolerance=±5% resistance=220 package=THT]
  CONN1 = SMA-15
  buzzer = BMT0905XH05

nets:
  N1: DC24V.GND, U1.3, U1.4, U2.3, U2.4
  N2: DC24V.PWR, U1.1, U1.2, U2.1, U2.2
  GND: 5Vto3V.GND, U1.5, U1.6, R1.Pin_0, R2.Pin_0, R3.Pin_0, R4.Pin_0, Part1.GND, BTM-112.GND, J1.pin1, U2.5, U2.6, LED1.cathode, LED2.cathode, CONN1.GND, buzzer.2
  3V3: 5Vto3V.LV, Part1.3V3, BTM-112.3V3
  N3: 5Vto3V.RX_LV, BTM-112.UART_TX
  N4: 5Vto3V.TX_LV, BTM-112.UART_RX
  N5: 5Vto3V.TX_HV, Part1.D3_PWM
  N6: 5Vto3V.RX_HV, Part1.D2
  N7: 5Vto3V.HV, S2.1, S3.1, S4.1, S1.1, Part1.5V, J1.pin2
  N8: S2.2, R2.Pin_1, Part1.A1
  N9: S3.2, R3.Pin_1, Part1.A2
  N10: S4.2, R4.Pin_1, Part1.A3
  N11: U1.7, Part1.D8
  N12: U1.8, Part1.D7
  N13: S1.2, R1.Pin_1, Part1.A0
  N14: Part1.A4/SDA, buzzer.1
  N15: Part1.A5/SCL, BTM-112.PIO6, R6.Pin_0
  N16: Part1.D9_PWM, J1.pin3
  N17: Part1.D5_PWM, U2.8
  N18: Part1.D6_PWM, U2.7
  N19: BTM-112.PIO7, R5.Pin_0
  N20: BTM-112.RF_IO, CONN1.SIGNAL
  N21: LED1.anode, R5.Pin_1
  N22: LED2.anode, R6.Pin_1

notes:
  plotter motors v1.1

custom parts:
  BTM-112: Bluetooth SMD module
  SMA-15: SMA 15 connector
  BMT0905XH05: Buzzer BMT0905XH05
